# Fritzing sketch gamecube-nunchuck-exercise (saved by Fritzing 0.9.3b)
breadboards: 1

parts:
  black_pill = IC, DIP package, 34 pins [chip_label=stm32f103c8]
  C1 = Electrolytic Capacitor [capacitance=10µF package="100 mil [THT, electrolytic]"]
  C2 = Ceramic Capacitor [capacitance=100nF package="100 mil [THT, multilayer]"]
  R1 = Resistor [tolerance=±5% resistance=220 package=THT]
  R2 = Resistor [tolerance=±5% resistance=220 package=THT]
  R3 = Resistor [tolerance=±5% resistance=220 package=THT]
  R4 = Resistor [tolerance=±5% resistance=220 package=THT]
  LED2 = LED - 5mm [color="Red (633nm)" package="5 mm [THT]"]
  LED3 = LED - 5mm [color="Red (633nm)" package="5 mm [THT]"]
  LED4 = LED - 5mm [color="Red (633nm)" package="5 mm [THT]"]
  LED5 = LED - 5mm [color="Red (633nm)" package="5 mm [THT]"]
  S1 = Pushbutton [package=THT]
  S2 = Pushbutton [package=THT]
  Gamecube_connector = shrouded pin header, 6 pins [form="♂ (shrouded male)"]
  R5 = Resistor [tolerance=±5% resistance=1k package=THT]
  exercise_+ = Header 1 [package=snap-male]
  exercise_GND = Header 1 [package=snap-male]  # not connected
  R6 = Resistor [tolerance=±5% resistance=100k package=THT]
  direction = Taiway 100-SP-X-T1 SPDT Miniature Toggle Switch [part_number=100-SP-X-T1-0-0-B1-M1 package=THT]
  R7 = Resistor [tolerance=±5% resistance=10k package=THT]
  R8 = Resistor [tolerance=±5% resistance=10k package=THT]
  Nunchuck_connector = shrouded pin header, 6 pins [form="♂ (shrouded male)"]

nets:
  N1: black_pill.pin5, direction.L2
  SCL: black_pill.pin14, R8.Pin_0, Nunchuck_connector.pin2
  SDA: black_pill.pin15, R7.Pin_0, Nunchuck_connector.pin5
  +3.3V: black_pill.pin16, C1.+, C2.1, LED2.anode, LED3.anode, LED4.anode, LED5.anode, S1.leg1, S2.leg1, Gamecube_connector.pin6, R5.Pin_0, R6.Pin_1, direction.COM, R7.Pin_1, R8.Pin_1, Nunchuck_connector.pin1
  GND/exercise ground/ground: black_pill.pin17, C1.-, C2.0, Gamecube_connector.pin3, Gamecube_connector.pin4, Nunchuck_connector.pin6
  N2: black_pill.pin23, R1.Pin_0
  N3: black_pill.pin24, R2.Pin_0
  N4: black_pill.pin25, R3.Pin_0
  N5: black_pill.pin26, R4.Pin_0
  N6: black_pill.pin27, S1.leg0
  N7: black_pill.pin28, S2.leg0
  N8: black_pill.pin29, Gamecube_connector.pin2, R5.Pin_1
  exercise +: black_pill.pin30, exercise_+.1, R6.Pin_0
  N9: R1.Pin_1, LED5.cathode
  N10: R2.Pin_1, LED4.cathode
  N11: R3.Pin_1, LED3.cathode
  N12: R4.Pin_1, LED2.cathode
